// Digital circuit ALU.dig as structural Verilog
module ALU (
  input  [15:0] a,
  input  [15:0] b,
  input  [2:0] ALUfunc,
  input  ci,
  output [15:0] Out,
  output Z,
  output N,
  output C,
  output V
);

  wire add_1_c_o, and_2_out, and_3_out, comparator_1_eq, comparator_2_eq, not_1_out, not_2_out, sub_1_c_o;
  wire [15:0] add_1_s, and_1_out, notconnected_1_out, or_1_out, shl_1_do, shr_1_do, sub_1_s, xor_1_out;

  Add #(.Bits(16)) add_1 (.a(a), .b(b), .c_i(ci), .s(add_1_s), .c_o(add_1_c_o));
  Sub #(.Bits(16)) sub_1 (.a(a), .b(b), .c_i(ci), .s(sub_1_s), .c_o(sub_1_c_o));
  assign and_1_out = a & b;  // And and_1, 16 bits wide
  assign or_1_out = a | b;  // Or or_1, 16 bits wide
  assign xor_1_out = a ^ b;  // XOr xor_1, 16 bits wide
  SHL shl_1 (.a(a), .b(b), .Do(shl_1_do));
  SHR shr_1 (.a(a), .b(b), .Do(shr_1_do));
  Comparator comparator_1 (.a(a[15]), .b(b[15]), .eq(comparator_1_eq));  // open: gt, lt
  Comparator comparator_2 (.a(a[15]), .b(Out[15]), .eq(comparator_2_eq));  // open: gt, lt
  not not_1 (not_1_out, comparator_2_eq);
  not not_2 (not_2_out, comparator_1_eq);
  Multiplexer #(.Selector_Bits(3), .Bits(16)) multiplexer_1 (
    .sel(ALUfunc), .in_0(add_1_s), .in_1(sub_1_s), .in_2(and_1_out), .in_3(or_1_out), .in_4(xor_1_out),
    .in_5(shl_1_do), .in_6(shr_1_do), .in_7(notconnected_1_out), .out(Out));
  // NotConnected on notconnected_1_out
  Multiplexer #(.Selector_Bits(3)) multiplexer_2 (
    .sel(ALUfunc), .in_0(add_1_c_o), .in_1(sub_1_c_o), .in_2(1'b0), .in_3(1'b0), .in_4(1'b0), .in_5(1'b0),
    .in_6(1'b0), .in_7(1'b0), .out(C));
  and and_2 (and_2_out, comparator_1_eq, not_1_out);
  and and_3 (and_3_out, not_2_out, not_1_out);
  Comparator #(.Signed("true"), .Bits(16)) comparator_3 (.a(Out), .b({16{1'b0}}), .eq(Z), .lt(N));  // open: gt
  Multiplexer #(.Selector_Bits(3)) multiplexer_3 (
    .sel(ALUfunc), .in_0(and_2_out), .in_1(and_3_out), .in_2(1'b0), .in_3(1'b0), .in_4(1'b0), .in_5(1'b0),
    .in_6(1'b0), .in_7(1'b0), .out(V));

  // Other names for the same wires on the sheet: Rd[15:0] = Out

  // Notes on the sheet:
  //   Out: ALU Result
  //   Z: Zero flag
  //   N: Negative flag
  //   C: Carry Flag
  //   V: Overfelow flag
  //   ALUfunc: Type of arthmatic operation
  //   ci: carry in
endmodule
