// Digital circuit ControlUnit.dig as structural Verilog
module ControlUnit (
  input  [3:0] Opcode,
  input  CondMet,
  output RegW,
  output MemWr,
  output MemRd,
  output ALUSrcA,
  output [1:0] ALUSrcB,
  output [1:0] WBSel,
  output [1:0] PCSrc,
  output RegDst,
  output [2:0] ALUFunc,
  output PC_abs,
  output IsNOP,
  output IsJR,
  output IsR,
  output IsSw
);

  wire B, comparator_1_gt, I_Addi, or_3_out, R_Add, R_And, R_Or, R_Shl, R_Shr, R_Sub, R_Xor, U_Lui;
  wire [0:0] or_4_out;

  Decoder #(.Selector_Bits(4)) decoder_1 (
    .sel(Opcode), .out_0(R_Add), .out_1(R_Sub), .out_2(R_And), .out_3(R_Or), .out_4(R_Xor), .out_5(R_Shl),
    .out_6(R_Shr), .out_7(I_Addi), .out_8(MemRd), .out_9(IsSw), .out_10(ALUSrcA), .out_11(U_Lui), .out_12(B),
    .out_13(RegDst), .out_14(IsJR), .out_15(IsNOP));
  or or_1 (IsR, R_Add, R_Sub, R_And, R_Or, R_Xor, R_Shl, R_Shr);
  or or_2 (ALUSrcB[0], I_Addi, MemRd, IsSw);
  and and_1 (PC_abs, IsJR, CondMet);
  or or_3 (or_3_out, IsR, I_Addi, MemRd, ALUSrcA, U_Lui, RegDst);
  and and_2 (MemWr, IsSw, CondMet);
  and and_3 (RegW, or_3_out, CondMet);
  or or_4 (or_4_out[0], RegDst, B);
  or or_5 (WBSel[0], MemRd, U_Lui);
  or or_6 (WBSel[1], RegDst, U_Lui);
  Comparator #(.Bits(4)) comparator_1 (.a(Opcode), .b(4'b0110), .gt(comparator_1_gt));  // open: eq, lt
  Multiplexer #(.Bits(3)) multiplexer_1 (.sel(comparator_1_gt), .in_0(Opcode[2:0]), .in_1(3'b000), .out(ALUFunc));
  Multiplexer #(.Bits(2)) multiplexer_2 (.sel(CondMet), .in_0(2'b00), .in_1({IsJR, or_4_out[0]}), .out(PCSrc));

  assign ALUSrcB[1] = ALUSrcA;

  // Other names for the same wires on the sheet: ALU_Func[2:0] = ALUFunc; Cond_Met = CondMet; I_Lw = MemRd;
  //   I_Sw = IsSw; IsI = ALUSrcB[0]; JAL = RegDst; JR = IsJR; NOP = IsNOP; ALU_Code[2:0] = Opcode[2:0];
  //   U_Movi = ALUSrcA
endmodule
