// Digital circuit FlagRegister.dig as structural Verilog
module FlagRegister (
  input  Zi,
  input  Ni,
  input  Ci,
  input  Vi,
  input  clk,
  input  SE,
  input  Reset,
  output Z,
  output N,
  output C,
  output V
);

  wire multiplexer_1_out, multiplexer_2_out, multiplexer_3_out, multiplexer_4_out, se_t;

  or or_1 (se_t, SE, Reset);
  Multiplexer multiplexer_1 (.sel(Reset), .in_0(Zi), .in_1(1'b0), .out(multiplexer_1_out));
  Multiplexer multiplexer_2 (.sel(Reset), .in_0(Ni), .in_1(1'b0), .out(multiplexer_2_out));
  Multiplexer multiplexer_3 (.sel(Reset), .in_0(Ci), .in_1(1'b0), .out(multiplexer_3_out));
  Multiplexer multiplexer_4 (.sel(Reset), .in_0(Vi), .in_1(1'b0), .out(multiplexer_4_out));
  Register register_1 (.D(multiplexer_1_out), .C(clk), .en(se_t), .Q(Z));
  Register register_2 (.D(multiplexer_2_out), .C(clk), .en(se_t), .Q(N));
  Register register_3 (.D(multiplexer_3_out), .C(clk), .en(se_t), .Q(C));
  Register register_4 (.D(multiplexer_4_out), .C(clk), .en(se_t), .Q(V));

  // Other names for the same wires on the sheet: rst = Reset

  // Notes on the sheet:
  //   Zi: Carry flag
  //   Ni: Negative flag input
  //   Ci: Carry input
  //   Vi: Overfelow input
  //   SE: Store flag in Registers
endmodule
