// Digital circuit PC.dig as structural Verilog
// The program counter.
// Here the current program counter is stored.
// The various inputs can be used to influence how the 
// program counter is modified if a clock signal happens.
// {{de Der Programmzähler. 
// Hier wird der aktuelle Programmzähler gespeichert. 
// Über die verschiedenen Eingänge kann beeinflußt 
// werden, auf welche Weise der Programmzähler mit 
// dem Takt weiter geschaltet wird.}}
module PC (
  input  [15:0] ShiftValue,
  input  C,
  input  reset,
  input  abs,
  output [7:0] Plus1,
  output [7:0] PC
);

  wire [7:0] Add_ALU_s, multiplexer_1_out, multiplexer_2_out;

  Multiplexer #(.Bits(8)) multiplexer_1 (
    .sel(reset), .in_0(multiplexer_2_out), .in_1({8{1'b0}}), .out(multiplexer_1_out));
  Register #(.Bits(8)) u_PC (.D(multiplexer_1_out), .C(C), .en(1'b1), .Q(PC));
  Add #(.Bits(8)) Add_One (.a(PC), .b(8'h1), .c_i(1'b0), .s(Plus1));  // open: c_o
  Add #(.Bits(8)) Add_ALU (.a(Plus1), .b(ShiftValue[7:0]), .c_i(1'b0), .s(Add_ALU_s));  // open: c_o
  Multiplexer #(.Bits(8)) multiplexer_2 (.sel(abs), .in_0(Add_ALU_s), .in_1(ShiftValue[7:0]), .out(multiplexer_2_out));

  // Notes on the sheet:
  //   ShiftValue: 16 bit shift value input
  //   Plus1: Address of the next instruction to execute.
  //   {{de Adresse des nächsten auszuführenden Befehls.}}
  //   PC: Programm Counter
  //   {{de Programmzähler}}
endmodule
