// Digital circuit Processor.dig as structural Verilog
module Processor (
  input  CLK,
  input  RESET,
  input  [2:0] DBG_RSEL,
  input  DBG_EN,
  input  [15:0] DBG_MADDR,
  output [7:0] PC_OUT,
  output [15:0] IR_OUT,
  output [3:0] FLAGS_OUT,
  output [15:0] DBG_ROUT,
  output [15:0] DBG_MOUT
);

  wire alu_1_c, alu_1_n, alu_1_v, alu_1_z, ALUSrcA, Cond_met, FR_En, IsJR, IsNOP, IsR, IsSw, MemRd, MemWr,
       multiplexer_7_out, not_1_out, or_1_out, PC_abs, RegDst, RegW;
  wire [1:0] ALUSrcB, PCSrc, WBSel;
  wire [2:0] ALUFunc, multiplexer_2_out, multiplexer_9_out, Rs1, Rs2;
  wire [7:0] PC_Plus1;
  wire [15:0] alu_1_out, ALU_a, ALU_b, multiplexer_1_out, multiplexer_5_out, multiplexer_6_out,
       notconnected_1_out, notconnected_2_out, PC_Plus1_16bit, RF_Rs1, SignExt_Imm4, SignExt_Imm7,
       SignExt_LUI, SignExt_Offset10;

  // NotConnected on notconnected_1_out
  Multiplexer #(.Selector_Bits(2), .Bits(16)) multiplexer_1 (
    .sel(PCSrc), .in_0({16{1'b0}}), .in_1(SignExt_Offset10), .in_2(RF_Rs1), .in_3(notconnected_1_out),
    .out(multiplexer_1_out));
  PC pc_1 (.ShiftValue(multiplexer_1_out), .C(CLK), .reset(RESET), .abs(PC_abs), .Plus1(PC_Plus1), .PC(PC_OUT));
  ROM #(.AddrBits(8), .isProgramMemory("true"), .Bits(16)) IMEM (.A(PC_OUT), .sel(1'b1), .D(IR_OUT));
  ControlUnit controlunit_1 (
    .Opcode(IR_OUT[13:10]), .CondMet(Cond_met), .RegW(RegW), .MemWr(MemWr), .MemRd(MemRd), .ALUSrcA(ALUSrcA),
    .ALUSrcB(ALUSrcB), .WBSel(WBSel), .PCSrc(PCSrc), .RegDst(RegDst), .ALUFunc(ALUFunc), .PC_abs(PC_abs),
    .IsNOP(IsNOP), .IsJR(IsJR), .IsR(IsR), .IsSw(IsSw));
  // Probe on IR_OUT[6:4]
  // Probe on IR_OUT[3:1]
  Multiplexer #(.Bits(3)) multiplexer_2 (.sel(RegDst), .in_0(IR_OUT[9:7]), .in_1(3'b111), .out(multiplexer_2_out));
  SignExt signext_1 (
    .imm4(IR_OUT[3:0]), .imm7(IR_OUT[6:0]), .offset10(IR_OUT[9:0]), .PC_Plus1(PC_Plus1),
    .imm4_out(SignExt_Imm4), .imm7_out(SignExt_Imm7), .offset10_out(SignExt_Offset10), .LUI_out(SignExt_LUI),
    .PCPlus1_16bit(PC_Plus1_16bit));
  RegisterFile registerfile_1 (
    .WD(multiplexer_6_out), .C(CLK), .S1(Rs1), .S2(Rs2), .WE(RegW), .Write_Addr(multiplexer_2_out),
    .Rs2(DBG_ROUT), .Rs1(RF_Rs1));
  // Probe on RF_Rs1
  // Probe on DBG_ROUT
  Multiplexer #(.Selector_Bits(2), .Bits(16)) multiplexer_3 (
    .sel(ALUSrcB), .in_0(DBG_ROUT), .in_1(SignExt_Imm4), .in_2(SignExt_Imm7), .in_3(notconnected_2_out),
    .out(ALU_b));
  // NotConnected on notconnected_2_out
  ALU alu_1 (
    .a(ALU_a), .b(ALU_b), .ALUfunc(ALUFunc), .ci(1'b0), .Out(alu_1_out), .Z(alu_1_z), .N(alu_1_n),
    .C(alu_1_c), .V(alu_1_v));
  // Probe on alu_1_out
  FlagRegister flagregister_1 (
    .Zi(alu_1_z), .Ni(alu_1_n), .Ci(alu_1_c), .Vi(alu_1_v), .clk(CLK), .SE(FR_En), .Reset(RESET),
    .Z(FLAGS_OUT[0]), .N(FLAGS_OUT[1]), .C(FLAGS_OUT[2]), .V(FLAGS_OUT[3]));
  Multiplexer #(.Bits(16)) multiplexer_4 (.sel(ALUSrcA), .in_0(RF_Rs1), .in_1({16{1'b0}}), .out(ALU_a));
  Multiplexer #(.Bits(16)) multiplexer_5 (.sel(DBG_EN), .in_0(alu_1_out), .in_1(DBG_MADDR), .out(multiplexer_5_out));
  Multiplexer #(.Selector_Bits(2), .Bits(16)) multiplexer_6 (
    .sel(WBSel), .in_0(alu_1_out), .in_1(DBG_MOUT), .in_2(PC_Plus1_16bit), .in_3(SignExt_LUI),
    .out(multiplexer_6_out));
  or or_1 (or_1_out, MemRd, DBG_EN);
  Multiplexer #(.Selector_Bits(2)) multiplexer_7 (
    .sel(IR_OUT[15:14]), .in_0(1'b1), .in_1(FLAGS_OUT[0]), .in_2(FLAGS_OUT[1]), .in_3(FLAGS_OUT[3]),
    .out(multiplexer_7_out));
  RAMDualPort #(.AddrBits(16), .Bits(16)) DMEM (
    .A(multiplexer_5_out), .Din(DBG_ROUT), .str(MemWr), .C(CLK), .ld(or_1_out), .D(DBG_MOUT));
  not not_1 (not_1_out, IsNOP);
  Multiplexer #(.Bits(3)) multiplexer_8 (.sel(IsJR), .in_0(IR_OUT[6:4]), .in_1(IR_OUT[9:7]), .out(Rs1));
  and and_1 (Cond_met, multiplexer_7_out, not_1_out);
  // Probe on Rs1
  Multiplexer #(.Bits(3)) multiplexer_9 (.sel(IsSw), .in_0(IR_OUT[3:1]), .in_1(IR_OUT[9:7]), .out(multiplexer_9_out));
  and and_2 (FR_En, IR_OUT[0], Cond_met, IsR);
  Multiplexer #(.Bits(3)) multiplexer_10 (.sel(DBG_EN), .in_0(multiplexer_9_out), .in_1(DBG_RSEL), .out(Rs2));
  // Probe on Rs2

  // Other names for the same wires on the sheet: Imm4_Inst[3:0] = IR_OUT[3:0]; Imm7_Inst[6:0] = IR_OUT[6:0];
  //   Offset10_Inst[9:0] = IR_OUT[9:0]; S_Inst = IR_OUT[0]; Rs2_Inst[2:0] = IR_OUT[3:1]; Rs1_Inst[2:0] = IR_OUT[6:4];
  //   Rd_Inst[2:0] = IR_OUT[9:7]; OpCode[3:0] = IR_OUT[13:10]; CC[1:0] = IR_OUT[15:14]; Mem_D[15:0] = DBG_MOUT;
  //   RF_Rs2[15:0] = DBG_ROUT
endmodule

/* Test case reset and fetch protocol:
CLK RESET DBG_EN DBG_RSEL DBG_MADDR PC_OUT IR_OUT FLAGS_OUT DBG_ROUT DBG_MOUT

program(0x2885,0x2909,0x0194,0x33ff)

0 0x0001 0 0 0 X X X X X
C 0x0001 0 0 0 X X X X X
# after reset the PC is 0 and the first instruction is visible
0 0 0 0 0 0x0000 0x2885 0x0000 X X
# one clock pulse == exactly one instruction
C 0 0 0 0 X X X X X
0 0 0 0 0 0x0001 0x2909 X X X
C 0 0 0 0 X X X X X
0 0 0 0 0 0x0002 0x0194 X X X
C 0 0 0 0 X X X X X
0 0 0 0 0 0x0003 0x33ff X X X
# HALT is a branch to itself, so the PC stays on it for ever
loop(i,20)
C 0 0 0 0 X X X X X
end loop
0 0 0 0 0 0x0003 0x33ff X X X
*/

/* Test case MOVI positive:
CLK RESET DBG_EN DBG_RSEL DBG_MADDR PC_OUT IR_OUT FLAGS_OUT DBG_ROUT DBG_MOUT

program(0x28bf,0x33ff)

0 0x0001 0 0 0 X X X X X
C 0x0001 0 0 0 X X X X X
loop(i,1)
C 0 0 0x0001 0 X X X X X
end loop
0 0 0x0001 0x0001 0 X X X 0x003f X
*/

/* Test case SHL:
CLK RESET DBG_EN DBG_RSEL DBG_MADDR PC_OUT IR_OUT FLAGS_OUT DBG_ROUT DBG_MOUT

program(0x2881,0x290f,0x1594,0x33ff)

0 0x0001 0 0 0 X X X X X
C 0x0001 0 0 0 X X X X X
loop(i,3)
C 0 0 0x0003 0 X X X X X
end loop
0 0 0x0001 0x0003 0 X X X 0x8000 X
*/

/* Test case no .S means the flags never change:
CLK RESET DBG_EN DBG_RSEL DBG_MADDR PC_OUT IR_OUT FLAGS_OUT DBG_ROUT DBG_MOUT

program(0x2887,0x2907,0x0595,0x2a01,0x2a82,0x074a,0x33ff)

0 0x0001 0 0 0 X X X X X
C 0x0001 0 0 0 X X X X X
loop(i,6)
C 0 0 0x0006 0 X X X X X
end loop
0 0 0x0001 0x0006 0 X X 0x0001 0xffff X
*/

/* Test case sum: all positive:
CLK RESET DBG_EN DBG_RSEL DBG_MADDR PC_OUT IR_OUT FLAGS_OUT DBG_ROUT DBG_MOUT

program(0x2890,0x2908,0x2a00,0x0421,0x7005,0x2190,0x0246,0x1c91,0x1d2f,0x33f9,0x2600,0x33ff)
memory DMEM(16) = 0x0005;
memory DMEM(17) = 0x0003;
memory DMEM(18) = 0x000c;
memory DMEM(19) = 0x0001;
memory DMEM(20) = 0x0028;
memory DMEM(21) = 0x0007;
memory DMEM(22) = 0x0002;
memory DMEM(23) = 0x001e;

0 0x0001 0 0 0 X X X X X
C 0x0001 0 0 0 X X X X X
0 0 0 0 0 0x0000 X X X X
loop(i,200)
C 0 0 0 0 X X X X X
end loop
# the program must have reached its final self-loop by now ...
0 0 0 0 0 0x000b X X X X
loop(i,5)
C 0 0 0 0 X X X X X
end loop
# ... and must stay there
0 0 0 0 0 0x000b X X X X
0 0 0x0001 0 0x0000 X X X X 0x0064
*/

/* Test case sort: random:
CLK RESET DBG_EN DBG_RSEL DBG_MADDR PC_OUT IR_OUT FLAGS_OUT DBG_ROUT DBG_MOUT

program(0x2890,0x2908,0x1d2f,0x0421,0x700e,0x0190,0x0314,0x043d,0xb001,0x33f8,0x2230,0x22b1,0x0459,0xb001,0x3002,0x26b0,0x2631,0x1db1,0x33f4,0x33ff)
memory DMEM(16) = 0x002a;
memory DMEM(17) = 0xfff9;
memory DMEM(18) = 0x0000;
memory DMEM(19) = 0x0384;
memory DMEM(20) = 0x0005;
memory DMEM(21) = 0x0005;
memory DMEM(22) = 0xffff;
memory DMEM(23) = 0x0080;

0 0x0001 0 0 0 X X X X X
C 0x0001 0 0 0 X X X X X
0 0 0 0 0 0x0000 X X X X
loop(i,1200)
C 0 0 0 0 X X X X X
end loop
# the program must have reached its final self-loop by now ...
0 0 0 0 0 0x0013 X X X X
loop(i,5)
C 0 0 0 0 X X X X X
end loop
# ... and must stay there
0 0 0 0 0 0x0013 X X X X
0 0 0x0001 0 0x0010 X X X X 0xfff9
0 0 0x0001 0 0x0011 X X X X 0xffff
0 0 0x0001 0 0x0012 X X X X 0x0000
0 0 0x0001 0 0x0013 X X X X 0x0005
0 0 0x0001 0 0x0014 X X X X 0x0005
0 0 0x0001 0 0x0015 X X X X 0x002a
0 0 0x0001 0 0x0016 X X X X 0x0080
0 0 0x0001 0 0x0017 X X X X 0x0384
*/

/* Test case far branches, forward and backward:
CLK RESET DBG_EN DBG_RSEL DBG_MADDR PC_OUT IR_OUT FLAGS_OUT DBG_ROUT DBG_MOUT

program(0x30c7,0x2907,0x33ff,0x0000,0x0000,0x0000,0x0000,0x0000,0x0000,0x0000,0x0000,0x0000,0x0000,0x0000,0x0000,0x0000,0x0000,0x0000,0x0000,0x0000,0x0000,0x0000,0x0000,0x0000,0x0000,0x0000,0x0000,0x0000,0x0000,0x0000,0x0000,0x0000,0x0000,0x0000,0x0000,0x0000,0x0000,0x0000,0x0000,0x0000,0x0000,0x0000,0x0000,0x0000,0x0000,0x0000,0x0000,0x0000,0x0000,0x0000,0x0000,0x0000,0x0000,0x0000,0x0000,0x0000,0x0000,0x0000,0x0000,0x0000,0x0000,0x0000,0x0000,0x0000,0x0000,0x0000,0x0000,0x0000,0x0000,0x0000,0x0000,0x0000,0x0000,0x0000,0x0000,0x0000,0x0000,0x0000,0x0000,0x0000,0x0000,0x0000,0x0000,0x0000,0x0000,0x0000,0x0000,0x0000,0x0000,0x0000,0x0000,0x0000,0x0000,0x0000,0x0000,0x0000,0x0000,0x0000,0x0000,0x0000,0x0000,0x0000,0x0000,0x0000,0x0000,0x0000,0x0000,0x0000,0x0000,0x0000,0x0000,0x0000,0x0000,0x0000,0x0000,0x0000,0x0000,0x0000,0x0000,0x0000,0x0000,0x0000,0x0000,0x0000,0x0000,0x0000,0x0000,0x0000,0x0000,0x0000,0x0000,0x0000,0x0000,0x0000,0x0000,0x0000,0x0000,0x0000,0x0000,0x0000,0x0000,0x0000,0x0000,0x0000,0x0000,0x0000,0x0000,0x0000,0x0000,0x0000,0x0000,0x0000,0x0000,0x0000,0x0000,0x0000,0x0000,0x0000,0x0000,0x0000,0x0000,0x0000,0x0000,0x0000,0x0000,0x0000,0x0000,0x0000,0x0000,0x0000,0x0000,0x0000,0x0000,0x0000,0x0000,0x0000,0x0000,0x0000,0x0000,0x0000,0x0000,0x0000,0x0000,0x0000,0x0000,0x0000,0x0000,0x0000,0x0000,0x0000,0x0000,0x0000,0x0000,0x0000,0x0000,0x0000,0x0000,0x0000,0x0000,0x0000,0x2883,0x3337)

0 0x0001 0 0 0 X X X X X
C 0x0001 0 0 0 X X X X X
0 0 0 0 0 0x0000 X X X X
C 0 0 0 0 X X X X X
# forward branch of +199 landed
0 0 0 0 0 0x00c8 X X X X
C 0 0 0 0 X X X X X
C 0 0 0 0 X X X X X
# backward branch of -201 landed
0 0 0 0 0 0x0001 X X X X
C 0 0 0 0 X X X X X
0 0 0x0001 0x0002 0 X X X 0x0007 X
*/

/* Test case MOVI negative (sign extended):
CLK RESET DBG_EN DBG_RSEL DBG_MADDR PC_OUT IR_OUT FLAGS_OUT DBG_ROUT DBG_MOUT

program(0x28c0,0x33ff)

0 0x0001 0 0 0 X X X X X
C 0x0001 0 0 0 X X X X X
loop(i,1)
C 0 0 0x0001 0 X X X X X
end loop
0 0 0x0001 0x0001 0 X X X 0xffc0 X
*/

/* Test case SHR:
CLK RESET DBG_EN DBG_RSEL DBG_MADDR PC_OUT IR_OUT FLAGS_OUT DBG_ROUT DBG_MOUT

program(0x2881,0x290f,0x1494,0x290c,0x1994,0x33ff)

0 0x0001 0 0 0 X X X X X
C 0x0001 0 0 0 X X X X X
loop(i,5)
C 0 0 0x0003 0 X X X X X
end loop
0 0 0x0001 0x0003 0 X X X 0x0008 X
*/

/* Test case LW and SW:
CLK RESET DBG_EN DBG_RSEL DBG_MADDR PC_OUT IR_OUT FLAGS_OUT DBG_ROUT DBG_MOUT

program(0x2890,0x2110,0x1d23,0x2511,0x33ff)
memory DMEM(16) = 0x0061;

0 0x0001 0 0 0 X X X X X
C 0x0001 0 0 0 X X X X X
loop(i,4)
C 0 0 0 0 X X X X X
end loop
0 0 0x0001 0x0002 0x0011 X X X 0x0064 0x0064
*/

/* Test case sum: mixed signs:
CLK RESET DBG_EN DBG_RSEL DBG_MADDR PC_OUT IR_OUT FLAGS_OUT DBG_ROUT DBG_MOUT

program(0x2890,0x2908,0x2a00,0x0421,0x7005,0x2190,0x0246,0x1c91,0x1d2f,0x33f9,0x2600,0x33ff)
memory DMEM(16) = 0xfffb;
memory DMEM(17) = 0x0003;
memory DMEM(18) = 0xfff4;
memory DMEM(19) = 0x0001;
memory DMEM(20) = 0xffd8;
memory DMEM(21) = 0x0007;
memory DMEM(22) = 0xfffe;
memory DMEM(23) = 0x001e;

0 0x0001 0 0 0 X X X X X
C 0x0001 0 0 0 X X X X X
0 0 0 0 0 0x0000 X X X X
loop(i,200)
C 0 0 0 0 X X X X X
end loop
# the program must have reached its final self-loop by now ...
0 0 0 0 0 0x000b X X X X
loop(i,5)
C 0 0 0 0 X X X X X
end loop
# ... and must stay there
0 0 0 0 0 0x000b X X X X
0 0 0x0001 0 0x0000 X X X X 0xffee
*/

/* Test case sort: already sorted:
CLK RESET DBG_EN DBG_RSEL DBG_MADDR PC_OUT IR_OUT FLAGS_OUT DBG_ROUT DBG_MOUT

program(0x2890,0x2908,0x1d2f,0x0421,0x700e,0x0190,0x0314,0x043d,0xb001,0x33f8,0x2230,0x22b1,0x0459,0xb001,0x3002,0x26b0,0x2631,0x1db1,0x33f4,0x33ff)
memory DMEM(16) = 0x0001;
memory DMEM(17) = 0x0002;
memory DMEM(18) = 0x0003;
memory DMEM(19) = 0x0004;
memory DMEM(20) = 0x0005;
memory DMEM(21) = 0x0006;
memory DMEM(22) = 0x0007;
memory DMEM(23) = 0x0008;

0 0x0001 0 0 0 X X X X X
C 0x0001 0 0 0 X X X X X
0 0 0 0 0 0x0000 X X X X
loop(i,1200)
C 0 0 0 0 X X X X X
end loop
# the program must have reached its final self-loop by now ...
0 0 0 0 0 0x0013 X X X X
loop(i,5)
C 0 0 0 0 X X X X X
end loop
# ... and must stay there
0 0 0 0 0 0x0013 X X X X
0 0 0x0001 0 0x0010 X X X X 0x0001
0 0 0x0001 0 0x0011 X X X X 0x0002
0 0 0x0001 0 0x0012 X X X X 0x0003
0 0 0x0001 0 0x0013 X X X X 0x0004
0 0 0x0001 0 0x0014 X X X X 0x0005
0 0 0x0001 0 0x0015 X X X X 0x0006
0 0 0x0001 0 0x0016 X X X X 0x0007
0 0 0x0001 0 0x0017 X X X X 0x0008
*/

/* Test case reset from the middle of a program:
CLK RESET DBG_EN DBG_RSEL DBG_MADDR PC_OUT IR_OUT FLAGS_OUT DBG_ROUT DBG_MOUT

program(0x2885,0x2909,0x0194,0x33ff)

0 0x0001 0 0 0 X X X X X
C 0x0001 0 0 0 X X X X X
loop(i,3)
C 0 0 0 0 X X X X X
end loop
0 0 0 0 0 0x0003 X X X X
0 0x0001 0 0 0 X X X X X
C 0x0001 0 0 0 X X X X X
0 0 0 0 0 0x0000 0x2885 0x0000 X X
*/

/* Test case LUI puts imm7 into bits 15..9:
CLK RESET DBG_EN DBG_RSEL DBG_MADDR PC_OUT IR_OUT FLAGS_OUT DBG_ROUT DBG_MOUT

program(0x2cc0,0x2d09,0x33ff)

0 0x0001 0 0 0 X X X X X
C 0x0001 0 0 0 X X X X X
loop(i,2)
C 0 0 0 0 X X X X X
end loop
0 0 0x0001 0x0001 0 X X X 0x8000 X
0 0 0x0001 0x0002 0 X X X 0x1200 X
*/

/* Test case NOP changes nothing:
CLK RESET DBG_EN DBG_RSEL DBG_MADDR PC_OUT IR_OUT FLAGS_OUT DBG_ROUT DBG_MOUT

program(0x2895,0x3c00,0x3c00,0x33ff)

0 0x0001 0 0 0 X X X X X
C 0x0001 0 0 0 X X X X X
loop(i,1)
C 0 0 0 0 X X X X X
end loop
0 0 0 0 0 0x0001 0x3c00 X X X
loop(i,2)
C 0 0 0 0 X X X X X
end loop
0 0 0x0001 0x0001 0 0x0003 X 0x0000 0x0015 X
*/

/* Test case R0 is hard wired to zero:
CLK RESET DBG_EN DBG_RSEL DBG_MADDR PC_OUT IR_OUT FLAGS_OUT DBG_ROUT DBG_MOUT

program(0x282a,0x33ff)

0 0x0001 0 0 0 X X X X X
C 0x0001 0 0 0 X X X X X
loop(i,1)
C 0 0 0x0000 0 X X X X X
end loop
0 0 0x0001 0x0000 0 X X X 0x0000 X
*/

/* Test case ADDI:
CLK RESET DBG_EN DBG_RSEL DBG_MADDR PC_OUT IR_OUT FLAGS_OUT DBG_ROUT DBG_MOUT

program(0x288a,0x1d18,0x33ff)

0 0x0001 0 0 0 X X X X X
C 0x0001 0 0 0 X X X X X
loop(i,2)
C 0 0 0x0002 0 X X X X X
end loop
0 0 0x0001 0x0002 0 X X X 0x0002 X
*/

/* Test case predicated execution (.EQ taken, .LT suppressed):
CLK RESET DBG_EN DBG_RSEL DBG_MADDR PC_OUT IR_OUT FLAGS_OUT DBG_ROUT DBG_MOUT

program(0x2887,0x2907,0x0415,0x2981,0x41b2,0x2a01,0x8242,0x33ff)

0 0x0001 0 0 0 X X X X X
C 0x0001 0 0 0 X X X X X
loop(i,7)
C 0 0 0 0 X X X X X
end loop
0 0 0x0001 0x0003 0 X X X 0x0008 X
0 0 0x0001 0x0004 0 X X X 0x0001 X
*/

/* Test case sum: all zero:
CLK RESET DBG_EN DBG_RSEL DBG_MADDR PC_OUT IR_OUT FLAGS_OUT DBG_ROUT DBG_MOUT

program(0x2890,0x2908,0x2a00,0x0421,0x7005,0x2190,0x0246,0x1c91,0x1d2f,0x33f9,0x2600,0x33ff)
memory DMEM(16) = 0x0000;
memory DMEM(17) = 0x0000;
memory DMEM(18) = 0x0000;
memory DMEM(19) = 0x0000;
memory DMEM(20) = 0x0000;
memory DMEM(21) = 0x0000;
memory DMEM(22) = 0x0000;
memory DMEM(23) = 0x0000;

0 0x0001 0 0 0 X X X X X
C 0x0001 0 0 0 X X X X X
0 0 0 0 0 0x0000 X X X X
loop(i,200)
C 0 0 0 0 X X X X X
end loop
# the program must have reached its final self-loop by now ...
0 0 0 0 0 0x000b X X X X
loop(i,5)
C 0 0 0 0 X X X X X
end loop
# ... and must stay there
0 0 0 0 0 0x000b X X X X
0 0 0x0001 0 0x0000 X X X X 0x0000
*/

/* Test case sort: reverse sorted:
CLK RESET DBG_EN DBG_RSEL DBG_MADDR PC_OUT IR_OUT FLAGS_OUT DBG_ROUT DBG_MOUT

program(0x2890,0x2908,0x1d2f,0x0421,0x700e,0x0190,0x0314,0x043d,0xb001,0x33f8,0x2230,0x22b1,0x0459,0xb001,0x3002,0x26b0,0x2631,0x1db1,0x33f4,0x33ff)
memory DMEM(16) = 0x0008;
memory DMEM(17) = 0x0007;
memory DMEM(18) = 0x0006;
memory DMEM(19) = 0x0005;
memory DMEM(20) = 0x0004;
memory DMEM(21) = 0x0003;
memory DMEM(22) = 0x0002;
memory DMEM(23) = 0x0001;

0 0x0001 0 0 0 X X X X X
C 0x0001 0 0 0 X X X X X
0 0 0 0 0 0x0000 X X X X
loop(i,1200)
C 0 0 0 0 X X X X X
end loop
# the program must have reached its final self-loop by now ...
0 0 0 0 0 0x0013 X X X X
loop(i,5)
C 0 0 0 0 X X X X X
end loop
# ... and must stay there
0 0 0 0 0 0x0013 X X X X
0 0 0x0001 0 0x0010 X X X X 0x0001
0 0 0x0001 0 0x0011 X X X X 0x0002
0 0 0x0001 0 0x0012 X X X X 0x0003
0 0 0x0001 0 0x0013 X X X X 0x0004
0 0 0x0001 0 0x0014 X X X X 0x0005
0 0 0x0001 0 0x0015 X X X X 0x0006
0 0 0x0001 0 0x0016 X X X X 0x0007
0 0 0x0001 0 0x0017 X X X X 0x0008
*/

/* Test case JR uses only the low 8 bits of Rs1:
CLK RESET DBG_EN DBG_RSEL DBG_MADDR PC_OUT IR_OUT FLAGS_OUT DBG_ROUT DBG_MOUT

program(0x2c89,0x1c97,0x3880,0x2981,0x2982,0x2983,0x2984,0x2989,0x33ff)

0 0x0001 0 0 0 X X X X X
C 0x0001 0 0 0 X X X X X
loop(i,3)
C 0 0 0 0 X X X X X
end loop
# only the low 8 bits of R1 reach the PC
0 0 0 0 0 0x0007 X X X X
C 0 0 0 0 X X X X X
0 0 0x0001 0x0003 0 X X X 0x0009 X
*/

/* Test case ADD:
CLK RESET DBG_EN DBG_RSEL DBG_MADDR PC_OUT IR_OUT FLAGS_OUT DBG_ROUT DBG_MOUT

program(0x2894,0x297b,0x0194,0x33ff)

0 0x0001 0 0 0 X X X X X
C 0x0001 0 0 0 X X X X X
loop(i,3)
C 0 0 0x0003 0 X X X X X
end loop
0 0 0x0001 0x0003 0 X X X 0x000f X
*/

/* Test case flags: zero:
CLK RESET DBG_EN DBG_RSEL DBG_MADDR PC_OUT IR_OUT FLAGS_OUT DBG_ROUT DBG_MOUT

program(0x2887,0x2907,0x0595,0x33ff)

0 0x0001 0 0 0 X X X X X
C 0x0001 0 0 0 X X X X X
loop(i,3)
C 0 0 0x0003 0 X X X X X
end loop
0 0 0x0001 0x0003 0 X X 0x0001 0x0000 X
*/

/* Test case conditional branch taken and not taken:
CLK RESET DBG_EN DBG_RSEL DBG_MADDR PC_OUT IR_OUT FLAGS_OUT DBG_ROUT DBG_MOUT

program(0x2887,0x2907,0x0415,0x2980,0x7001,0x29bc,0x2a05,0xb001,0x2a81,0x33ff)

0 0x0001 0 0 0 X X X X X
C 0x0001 0 0 0 X X X X X
loop(i,10)
C 0 0 0 0 X X X X X
end loop
0 0 0x0001 0x0003 0 X X X 0x0000 X
0 0 0x0001 0x0005 0 X X X 0x0001 X
*/

/* Test case sort: all equal:
CLK RESET DBG_EN DBG_RSEL DBG_MADDR PC_OUT IR_OUT FLAGS_OUT DBG_ROUT DBG_MOUT

program(0x2890,0x2908,0x1d2f,0x0421,0x700e,0x0190,0x0314,0x043d,0xb001,0x33f8,0x2230,0x22b1,0x0459,0xb001,0x3002,0x26b0,0x2631,0x1db1,0x33f4,0x33ff)
memory DMEM(16) = 0x0004;
memory DMEM(17) = 0x0004;
memory DMEM(18) = 0x0004;
memory DMEM(19) = 0x0004;
memory DMEM(20) = 0x0004;
memory DMEM(21) = 0x0004;
memory DMEM(22) = 0x0004;
memory DMEM(23) = 0x0004;

0 0x0001 0 0 0 X X X X X
C 0x0001 0 0 0 X X X X X
0 0 0 0 0 0x0000 X X X X
loop(i,1200)
C 0 0 0 0 X X X X X
end loop
# the program must have reached its final self-loop by now ...
0 0 0 0 0 0x0013 X X X X
loop(i,5)
C 0 0 0 0 X X X X X
end loop
# ... and must stay there
0 0 0 0 0 0x0013 X X X X
0 0 0x0001 0 0x0010 X X X X 0x0004
0 0 0x0001 0 0x0011 X X X X 0x0004
0 0 0x0001 0 0x0012 X X X X 0x0004
0 0 0x0001 0 0x0013 X X X X 0x0004
0 0 0x0001 0 0x0014 X X X X 0x0004
0 0 0x0001 0 0x0015 X X X X 0x0004
0 0 0x0001 0 0x0016 X X X X 0x0004
0 0 0x0001 0 0x0017 X X X X 0x0004
*/

/* Test case JAL saves the return address in R7:
CLK RESET DBG_EN DBG_RSEL DBG_MADDR PC_OUT IR_OUT FLAGS_OUT DBG_ROUT DBG_MOUT

program(0x3402,0x2905,0x33ff,0x2a08,0x3b80)

0 0x0001 0 0 0 X X X X X
C 0x0001 0 0 0 X X X X X
0 0 0 0 0 0x0000 X X X X
C 0 0 0 0 X X X X X
# jumped into the subroutine
0 0 0 0 0 0x0003 X X X X
C 0 0 0 0 X X X X X
C 0 0 0 0 X X X X X
# and came back to the instruction after JAL
0 0 0 0 0 0x0001 X X X X
C 0 0 0 0 X X X X X
# R7 holds PC+1 of the JAL, zero extended into 16 bits
0 0 0x0001 0x0007 0 X X X 0x0001 X
0 0 0x0001 0x0004 0 X X X 0x0008 X
0 0 0x0001 0x0002 0 X X X 0x0005 X
*/

/* Test case SUB:
CLK RESET DBG_EN DBG_RSEL DBG_MADDR PC_OUT IR_OUT FLAGS_OUT DBG_ROUT DBG_MOUT

program(0x2894,0x297b,0x0594,0x33ff)

0 0x0001 0 0 0 X X X X X
C 0x0001 0 0 0 X X X X X
loop(i,3)
C 0 0 0x0003 0 X X X X X
end loop
0 0 0x0001 0x0003 0 X X X 0x0019 X
*/

/* Test case flags: negative and borrow:
CLK RESET DBG_EN DBG_RSEL DBG_MADDR PC_OUT IR_OUT FLAGS_OUT DBG_ROUT DBG_MOUT

program(0x2883,0x2905,0x0595,0x33ff)

0 0x0001 0 0 0 X X X X X
C 0x0001 0 0 0 X X X X X
loop(i,3)
C 0 0 0x0003 0 X X X X X
end loop
0 0 0x0001 0x0003 0 X X 0x0006 0xfffe X
*/

/* Test case sort: extremes:
CLK RESET DBG_EN DBG_RSEL DBG_MADDR PC_OUT IR_OUT FLAGS_OUT DBG_ROUT DBG_MOUT

program(0x2890,0x2908,0x1d2f,0x0421,0x700e,0x0190,0x0314,0x043d,0xb001,0x33f8,0x2230,0x22b1,0x0459,0xb001,0x3002,0x26b0,0x2631,0x1db1,0x33f4,0x33ff)
memory DMEM(16) = 0x03e8;
memory DMEM(17) = 0xfc18;
memory DMEM(18) = 0x03e7;
memory DMEM(19) = 0xfc19;
memory DMEM(20) = 0x0000;
memory DMEM(21) = 0x0001;
memory DMEM(22) = 0xffff;
memory DMEM(23) = 0x01f4;

0 0x0001 0 0 0 X X X X X
C 0x0001 0 0 0 X X X X X
0 0 0 0 0 0x0000 X X X X
loop(i,1200)
C 0 0 0 0 X X X X X
end loop
# the program must have reached its final self-loop by now ...
0 0 0 0 0 0x0013 X X X X
loop(i,5)
C 0 0 0 0 X X X X X
end loop
# ... and must stay there
0 0 0 0 0 0x0013 X X X X
0 0 0x0001 0 0x0010 X X X X 0xfc18
0 0 0x0001 0 0x0011 X X X X 0xfc19
0 0 0x0001 0 0x0012 X X X X 0xffff
0 0 0x0001 0 0x0013 X X X X 0x0000
0 0 0x0001 0 0x0014 X X X X 0x0001
0 0 0x0001 0 0x0015 X X X X 0x01f4
0 0 0x0001 0 0x0016 X X X X 0x03e7
0 0 0x0001 0 0x0017 X X X X 0x03e8
*/

/* Test case a predicated JAL that is not taken writes nothing:
CLK RESET DBG_EN DBG_RSEL DBG_MADDR PC_OUT IR_OUT FLAGS_OUT DBG_ROUT DBG_MOUT

program(0x2b95,0x2883,0x2904,0x0415,0x7401,0x2a86,0x33ff)

0 0x0001 0 0 0 X X X X X
C 0x0001 0 0 0 X X X X X
loop(i,5)
C 0 0 0 0 X X X X X
end loop
# the conditional JAL was skipped, so R7 still holds the sentinel
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*/

/* Test case AND / OR / XOR:
CLK RESET DBG_EN DBG_RSEL DBG_MADDR PC_OUT IR_OUT FLAGS_OUT DBG_ROUT DBG_MOUT

program(0x288c,0x290a,0x0994,0x0e14,0x1294,0x33ff)

0 0x0001 0 0 0 X X X X X
C 0x0001 0 0 0 X X X X X
loop(i,5)
C 0 0 0x0005 0 X X X X X
end loop
0 0 0x0001 0x0005 0 X X X 0x0006 X
*/

/* Test case flags: signed overflow:
CLK RESET DBG_EN DBG_RSEL DBG_MADDR PC_OUT IR_OUT FLAGS_OUT DBG_ROUT DBG_MOUT

program(0x2881,0x290f,0x1494,0x0193,0x33ff)

0 0x0001 0 0 0 X X X X X
C 0x0001 0 0 0 X X X X X
loop(i,4)
C 0 0 0x0003 0 X X X X X
end loop
0 0 0x0001 0x0003 0 X X 0x000d 0x0000 X
*/
