// Digital circuit RegisterFile.dig as structural Verilog
module RegisterFile (
  input  [15:0] WD,
  input  C,
  input  [2:0] S1,
  input  [2:0] S2,
  input  WE,
  input  [2:0] Write_Addr,
  output [15:0] Rs2,
  output [15:0] Rs1
);

  wire demultiplexer_1_out_0, demultiplexer_1_out_1, demultiplexer_1_out_2, demultiplexer_1_out_3,
       demultiplexer_1_out_4, demultiplexer_1_out_5, demultiplexer_1_out_6, demultiplexer_1_out_7;
  wire [15:0] R0_q, R1_q, R2_q, R3_q, R4_q, R5_q, R6_q, R7_q;

  Demultiplexer #(.Selector_Bits(3)) demultiplexer_1 (
    .sel(Write_Addr), .in(WE), .out_0(demultiplexer_1_out_0), .out_1(demultiplexer_1_out_1),
    .out_2(demultiplexer_1_out_2), .out_3(demultiplexer_1_out_3), .out_4(demultiplexer_1_out_4),
    .out_5(demultiplexer_1_out_5), .out_6(demultiplexer_1_out_6), .out_7(demultiplexer_1_out_7));
  Register #(.Bits(16)) R0 (.D({16{1'b0}}), .C(C), .en(demultiplexer_1_out_0), .Q(R0_q));
  Register #(.Bits(16)) R1 (.D(WD), .C(C), .en(demultiplexer_1_out_1), .Q(R1_q));
  Register #(.Bits(16)) R2 (.D(WD), .C(C), .en(demultiplexer_1_out_2), .Q(R2_q));
  Register #(.Bits(16)) R3 (.D(WD), .C(C), .en(demultiplexer_1_out_3), .Q(R3_q));
  Register #(.Bits(16)) R4 (.D(WD), .C(C), .en(demultiplexer_1_out_4), .Q(R4_q));
  Register #(.Bits(16)) R5 (.D(WD), .C(C), .en(demultiplexer_1_out_5), .Q(R5_q));
  Register #(.Bits(16)) R6 (.D(WD), .C(C), .en(demultiplexer_1_out_6), .Q(R6_q));
  Register #(.Bits(16)) R7 (.D(WD), .C(C), .en(demultiplexer_1_out_7), .Q(R7_q));
  Multiplexer #(.Selector_Bits(3), .Bits(16)) multiplexer_1 (
    .sel(S2), .in_0(R0_q), .in_1(R1_q), .in_2(R2_q), .in_3(R3_q), .in_4(R4_q), .in_5(R5_q), .in_6(R6_q),
    .in_7(R7_q), .out(Rs2));
  Multiplexer #(.Selector_Bits(3), .Bits(16)) multiplexer_2 (
    .sel(S1), .in_0(R0_q), .in_1(R1_q), .in_2(R2_q), .in_3(R3_q), .in_4(R4_q), .in_5(R5_q), .in_6(R6_q),
    .in_7(R7_q), .out(Rs1));
  // also tied to GND on the sheet: {R0_q[0], R0_q[1], R0_q[2], R0_q[3], R0_q[4], R0_q[5], R0_q[6], R0_q[7], R0_q[8], R0_q[9], R0_q[10], R0_q[11], R0_q[12], R0_q[13], R0_q[14], R0_q[15]}

  // Notes on the sheet:
  //   WD: Data to be stored.
  //   The value applied here is stored when the input WE is set to 1.
  //   {{de Daten die gespeichert werden sollen.
  //   Der hier anliegende Wert wird gespeichert, wenn 
  //   der Eingang WE auf 1 geschaltet wird.}}
  //   Rs2: Contents of the Destignation Register.
  //   Which register is output is determined by 
  //   the input dest.
  //   {{de  Inhalt des Destignation Registers.
  //   Welches Register ausgegeben wird, wird mittels 
  //   des Eingangs dest festgelegt.}}
  //   Rs1: Contents of the Source Register.
  //   Which register is output is determined by the input src.
  //   {{de Inhalt des Source Registers. Welches Register
  //   ausgegeben wird, wird mittels des Einganges src
  //   festgelegt.}}
  //   WE: Activate storing. When this input is high, the value at WD is 
  //   stored in the register specified in dest at the next clock signal.
  //   {{de Das Speichern aktivieren. Wenn dieser Eingang auf 
  //   High geht, wird der Wert an WD in dem Register 
  //   gespeichert, welches in dest angegeben ist.}}
endmodule
