// Digital circuit SHL.dig as structural Verilog
module SHL (
  input  [15:0] a,
  input  [15:0] b,
  output [15:0] Do
);

  BarrelShifter #(.Bits(16)) barrelshifter_1 (.in(a), .shift({1'b0, b[3:0]}), .out(Do));

  // Notes on the sheet:
  //   a: Input to be shifted
  //   b: Amount of shift Rs2[3:0]
  //   Do: Shifted a
endmodule
