// Digital circuit SHR.dig as structural Verilog
module SHR (
  input  [15:0] a,
  input  [15:0] b,
  output [15:0] Do
);

  BarrelShifter #(.Bits(16), .direction("right")) barrelshifter_1 (.in(a), .shift({1'b0, b[3:0]}), .out(Do));
endmodule
