// Digital circuit SignExt.dig as structural Verilog
module SignExt (
  input  [3:0] imm4,
  input  [6:0] imm7,
  input  [9:0] offset10,
  input  [7:0] PC_Plus1,
  output [15:0] imm4_out,
  output [15:0] imm7_out,
  output [15:0] offset10_out,
  output [15:0] LUI_out,
  output [15:0] PCPlus1_16bit
);

  BitExtender #(.inputBits(4)) bitextender_1 (.in(imm4), .out(imm4_out));
  BitExtender #(.inputBits(7)) bitextender_2 (.in(imm7), .out(imm7_out));
  BitExtender #(.inputBits(10)) bitextender_3 (.in(offset10), .out(offset10_out));

  assign LUI_out = {imm7, {9{1'b0}}};
  assign PCPlus1_16bit = {{8{1'b0}}, PC_Plus1};

  // Notes on the sheet:
  //   PC_Plus1: 8 bit PC+1
  //   PCPlus1_16bit: 16 bit PC+1
endmodule
